# Fritzing sketch hotline_fritzing (saved by Fritzing 0.9.5d)
circuit board: 3.5cm x 5.99718cm

parts:
  DIAL = molex pin header, 3 pins [form=molex]
  PANEL = molex pin header, 3 pins [form=molex]
  AMP = molex pin header, 3 pins [form=molex]
  PHONE = molex pin header, 2 pins [form=molex]
  CRADLE = molex pin header, 2 pins [form=molex]
  AUDIO = female pin header, 1 pin [form="♀ (female)"]
  R1 = Resistor [tolerance=±5% resistance=220 package=THT]
  R2 = Resistor [tolerance=±5% resistance=220 package=THT]
  R3 = Resistor [tolerance=±5% resistance=220 package=THT]
  R4 = Resistor [tolerance=±5% resistance=220 package=THT]
  R5 = Resistor [tolerance=±5% resistance=220 package=THT]
  ORANGEPI = double row female pin header, 26 pins [form="♀ (female)"]
  PWR = molex pin header, 2 pins [form=molex]
  C1 = Electrolytic Capacitor [capacitance=100µF voltage=10V package="100 mil [THT, electrolytic]"]
  Q1 = Basic FET N-Channel [package="TO220 [THT]"]

nets:
  OPI21: DIAL.pin1, R3.Pin_1, ORANGEPI.pin21
  GND: DIAL.pin2, PANEL.pin2, PHONE.pin1, CRADLE.pin2, ORANGEPI.pin26, PWR.pin1, C1.-, Q1.source
  OPI17: DIAL.pin3, R4.Pin_1, ORANGEPI.pin17
  OPI16: PANEL.pin1, R5.Pin_0, ORANGEPI.pin16
  OPI15: PANEL.pin3, ORANGEPI.pin15
  AUDIO: AMP.pin1, PHONE.pin2, AUDIO.pin1
  N1: AMP.pin2, Q1.drain
  5V: AMP.pin3, ORANGEPI.pin12, ORANGEPI.pin13, PWR.pin2, C1.+
  OPI1: CRADLE.pin1, R1.Pin_1, ORANGEPI.pin1
  3.3V: R1.Pin_0, R3.Pin_0, R4.Pin_0, R5.Pin_1, ORANGEPI.pin14
  OPI23: R2.Pin_0, ORANGEPI.pin23
  N2: R2.Pin_1, Q1.gate

notes:
  THE LINE Adapter Board
